# Fritzing sketch GaggiaPIDController (saved by Fritzing 0.9.4)
circuit board: 8.46667cm x 5.64444cm
breadboards: 1

parts:
  Part1 = Arduino Nano (Rev3.0)
  U1 = RELAY-SOLIDSTATE [package=relay-s108t02]
  S2 = SWITCH-DPDT [package=os]
  Grove1 = Grove OLED 128x96
  U2 = MAX6675 [package=so08]
  U3 = MAX6675 [package=so08]
  R2 = Resistor [tolerance=±5% resistance=220 package="0603 [SMD]"]
  R1 = Resistor [tolerance=±5% resistance=220 package="0603 [SMD]"]

nets:
  GND: Part1.GND, U1.-, S2.6, Grove1.GND, U2.VSS, U3.VSS
  N1: Part1.D4, U2.CS
  N2: Part1.D5, U3.CS
  N3: Part1.D6, U1.+
  N4: Part1.D7, S2.1
  N5: Part1.D8, U2.SCK, U3.SCK
  N6: Part1.D9, U2.MISO, U3.MISO
  VDD: Part1.VIN, Grove1.VCC, U2.VDD, U3.VDD, R2.Pin_1, R1.Pin_1
  N7: Part1.A5, Grove1.SDA, R2.Pin_0
  N8: Part1.A4, Grove1.SCL, R1.Pin_0

notes:
  SSR: the other pins are connected to the heater
  Steam switch
  3.3K pull up resistors
  Steam sensor
  Water sensor
